// Logisim project tictactoe.circ as structural Verilog: 4 circuits, main circuit main
module main (
);

  wire button_1_out, button_2_out, button_3_out, button_4_out, button_5_out, button_6_out, button_7_out,
       button_8_out, button_9_out, button_10_out, juego_1_out_11, juego_1_out_12, juego_1_out_13,
       juego_1_out_14, juego_1_out_15, juego_1_out_16, juego_1_out_17, juego_1_out_18, juego_1_out_19,
       juego_1_out_20, juego_1_out_21, juego_1_out_22, juego_1_out_23, juego_1_out_24, juego_1_out_25,
       juego_1_out_26, juego_1_out_27, juego_1_out_28, juego_1_out_29, juego_1_out_30, juego_1_out_31;

  Button button_1 (.out(button_1_out));
  Button button_2 (.out(button_2_out));
  Button button_3 (.out(button_3_out));
  Button button_4 (.out(button_4_out));
  Button button_5 (.out(button_5_out));
  Button button_6 (.out(button_6_out));
  Button button_7 (.out(button_7_out));
  Button button_8 (.out(button_8_out));
  Button button_9 (.out(button_9_out));
  LED led_1 (.in(juego_1_out_13));
  LED led_2 (.in(juego_1_out_12));
  LED led_3 (.in(juego_1_out_11));
  juego juego_1 (
    .out_11(juego_1_out_11), .out_13(juego_1_out_13), .in_1(button_1_out), .in_2(button_4_out),
    .in_3(button_7_out), .in_4(button_2_out), .in_5(button_5_out), .in_6(button_8_out), .in_7(button_3_out),
    .in_8(button_6_out), .in_9(button_9_out), .in_10(button_10_out), .out_12(juego_1_out_12),
    .out_14(juego_1_out_14), .out_15(juego_1_out_15), .out_16(juego_1_out_16), .out_17(juego_1_out_17),
    .out_18(juego_1_out_18), .out_19(juego_1_out_19), .out_20(juego_1_out_20), .out_21(juego_1_out_21),
    .out_22(juego_1_out_22), .out_23(juego_1_out_23), .out_24(juego_1_out_24), .out_25(juego_1_out_25),
    .out_26(juego_1_out_26), .out_27(juego_1_out_27), .out_28(juego_1_out_28), .out_29(juego_1_out_29),
    .out_30(juego_1_out_30), .out_31(juego_1_out_31));
  LED led_4 (.in(juego_1_out_14));
  LED led_5 (.in(juego_1_out_20));
  LED led_6 (.in(juego_1_out_26));
  Button button_10 (.out(button_10_out));
  LED led_7 (.in(juego_1_out_16));
  LED led_8 (.in(juego_1_out_15));
  LED led_9 (.in(juego_1_out_22));
  LED led_10 (.in(juego_1_out_21));
  LED led_11 (.in(juego_1_out_28));
  LED led_12 (.in(juego_1_out_27));
  LED led_13 (.in(juego_1_out_17));
  LED led_14 (.in(juego_1_out_19));
  LED led_15 (.in(juego_1_out_18));
  LED led_16 (.in(juego_1_out_24));
  LED led_17 (.in(juego_1_out_25));
  LED led_18 (.in(juego_1_out_23));
  LED led_19 (.in(juego_1_out_29));
  LED led_20 (.in(juego_1_out_30));
  LED led_21 (.in(juego_1_out_31));

  // Notes on the sheet:
  //   1
  //   4
  //   7
  //   2
  //   5
  //   8
  //   oyuna 1. oyuncu başlar
  //   3
  //   6
  //   9
  //   XXX ya da OOO olunca(çapraz sütun satır) oyun kazanılıyor
  //   Oyun kazanıldıktan sonra resetlenmeli aksi takdirde ledleri yakamayız
  //   1. oyuncunun ledi sarı renk , 2. oyuncunun ledi yeşil renk
  //   1.oyuncu
  //   2.oyuncu
  //   berabere
  //   Reset
endmodule

module pozisyon (
  input  in_1,
  input  in_2,
  input  in_3,
  input  in_4,
  input  in_5,
  input  in_6,
  output out_7,
  output out_8,
  output out_9,
  output out_10
);

  wire d_ff_1_q;

  D_Flip_Flop d_ff_1 (.clk(in_2), .D(in_3), .Q(d_ff_1_q), .preset(in_4), .reset(in_5));  // open: Qn, en
  D_Flip_Flop d_ff_2 (.clk(d_ff_1_q), .D(in_1), .Q(out_7), .preset(in_4), .reset(in_5));  // open: Qn, en
  D_Flip_Flop d_ff_3 (.clk(d_ff_1_q), .D(in_6), .Q(out_9), .preset(in_4), .reset(in_5));  // open: Qn, en

  assign out_8 = out_7;
  assign out_10 = out_9;
endmodule

module juego (
  input  in_1,
  input  in_2,
  input  in_3,
  input  in_4,
  input  in_5,
  input  in_6,
  input  in_7,
  input  in_8,
  input  in_9,
  input  in_10,
  output out_11,
  output out_12,
  output out_13,
  output out_14,
  output out_15,
  output out_16,
  output out_17,
  output out_18,
  output out_19,
  output out_20,
  output out_21,
  output out_22,
  output out_23,
  output out_24,
  output out_25,
  output out_26,
  output out_27,
  output out_28,
  output out_29,
  output out_30,
  output out_31
);

  wire _1_out, _2_out, _3_out, _4_out, _5_out, _6_out, _7_out, _8_out, _9_out, and_1_out, and_2_out,
       and_3_out, and_4_out, and_5_out, ganador_1_out_10, ganador_2_out_10, not_3_out, pozisyon_1_out_7,
       pozisyon_1_out_9, pozisyon_2_out_7, pozisyon_2_out_9, pozisyon_3_out_7, pozisyon_3_out_9,
       pozisyon_4_out_7, pozisyon_4_out_9, pozisyon_5_out_7, pozisyon_5_out_9, pozisyon_6_out_7,
       pozisyon_6_out_9, pozisyon_7_out_7, pozisyon_7_out_9, pozisyon_8_out_7, pozisyon_8_out_9,
       pozisyon_9_out_7, pozisyon_9_out_9, xor_1_out, xor_2_out, xor_3_out, xor_4_out, xor_5_out, xor_6_out,
       xor_7_out, xor_8_out, xor_9_out, xor_10_out, xor_11_out, xor_12_out, xor_13_out, xor_14_out,
       xor_15_out, xor_16_out, xor_17_out;

  and _3 (_3_out, in_1, and_4_out);
  and _2 (_2_out, in_2, and_4_out);
  and _1 (_1_out, in_3, and_4_out);
  and _6 (_6_out, in_4, and_4_out);
  and _5 (_5_out, in_5, and_4_out);
  and _4 (_4_out, in_6, and_4_out);
  and _9 (_9_out, in_7, and_4_out);
  and _8 (_8_out, in_8, and_4_out);
  and _7 (_7_out, in_9, and_4_out);
  pozisyon pozisyon_1 (
    .in_1(not_3_out), .in_2(_3_out), .in_3(1'b1), .in_4(1'b0), .in_5(in_10), .in_6(xor_17_out),
    .out_7(pozisyon_1_out_7), .out_8(out_14), .out_9(pozisyon_1_out_9), .out_10(out_15));
  pozisyon pozisyon_2 (
    .in_1(not_3_out), .in_2(_2_out), .in_3(1'b1), .in_4(1'b0), .in_5(in_10), .in_6(xor_17_out),
    .out_7(pozisyon_2_out_7), .out_8(out_16), .out_9(pozisyon_2_out_9), .out_10(out_17));
  pozisyon pozisyon_3 (
    .in_1(not_3_out), .in_2(_1_out), .in_3(1'b1), .in_4(1'b0), .in_5(in_10), .in_6(xor_17_out),
    .out_7(pozisyon_3_out_7), .out_8(out_18), .out_9(pozisyon_3_out_9), .out_10(out_19));
  pozisyon pozisyon_4 (
    .in_1(not_3_out), .in_2(_6_out), .in_3(1'b1), .in_4(1'b0), .in_5(in_10), .in_6(xor_17_out),
    .out_7(pozisyon_4_out_7), .out_8(out_20), .out_9(pozisyon_4_out_9), .out_10(out_21));
  pozisyon pozisyon_5 (
    .in_1(not_3_out), .in_2(_5_out), .in_3(1'b1), .in_4(1'b0), .in_5(in_10), .in_6(xor_17_out),
    .out_7(pozisyon_5_out_7), .out_8(out_22), .out_9(pozisyon_5_out_9), .out_10(out_23));
  pozisyon pozisyon_6 (
    .in_1(not_3_out), .in_2(_4_out), .in_3(1'b1), .in_4(1'b0), .in_5(in_10), .in_6(xor_17_out),
    .out_7(pozisyon_6_out_7), .out_8(out_24), .out_9(pozisyon_6_out_9), .out_10(out_25));
  pozisyon pozisyon_7 (
    .in_1(not_3_out), .in_2(_9_out), .in_3(1'b1), .in_4(1'b0), .in_5(in_10), .in_6(xor_17_out),
    .out_7(pozisyon_7_out_7), .out_8(out_26), .out_9(pozisyon_7_out_9), .out_10(out_27));
  pozisyon pozisyon_8 (
    .in_1(not_3_out), .in_2(_8_out), .in_3(1'b1), .in_4(1'b0), .in_5(in_10), .in_6(xor_17_out),
    .out_7(pozisyon_8_out_7), .out_8(out_28), .out_9(pozisyon_8_out_9), .out_10(out_29));
  pozisyon pozisyon_9 (
    .in_1(not_3_out), .in_2(_7_out), .in_3(1'b1), .in_4(1'b0), .in_5(in_10), .in_6(xor_17_out),
    .out_7(pozisyon_9_out_7), .out_8(out_30), .out_9(pozisyon_9_out_9), .out_10(out_31));
  not not_1 (out_11, ganador_1_out_10);
  not not_2 (out_13, ganador_2_out_10);
  ganador ganador_1 (
    ._3(pozisyon_1_out_7), ._2(pozisyon_2_out_7), ._1(pozisyon_3_out_7), ._6(pozisyon_4_out_7),
    ._5(pozisyon_5_out_7), ._4(pozisyon_6_out_7), ._9(pozisyon_7_out_7), ._8(pozisyon_8_out_7),
    ._7(pozisyon_9_out_7), .out_10(ganador_1_out_10));
  ganador ganador_2 (
    ._3(pozisyon_1_out_9), ._2(pozisyon_2_out_9), ._1(pozisyon_3_out_9), ._6(pozisyon_4_out_9),
    ._5(pozisyon_5_out_9), ._4(pozisyon_6_out_9), ._9(pozisyon_7_out_9), ._8(pozisyon_8_out_9),
    ._7(pozisyon_9_out_9), .out_10(ganador_2_out_10));
  xor xor_1 (xor_1_out, pozisyon_1_out_7, pozisyon_1_out_9);
  xor xor_2 (xor_2_out, pozisyon_9_out_7, pozisyon_9_out_9);
  xor xor_3 (xor_3_out, pozisyon_2_out_7, pozisyon_2_out_9);
  xor xor_4 (xor_4_out, pozisyon_3_out_7, pozisyon_3_out_9);
  xor xor_5 (xor_5_out, pozisyon_4_out_7, pozisyon_4_out_9);
  xor xor_6 (xor_6_out, pozisyon_5_out_7, pozisyon_5_out_9);
  xor xor_7 (xor_7_out, pozisyon_6_out_7, pozisyon_6_out_9);
  xor xor_8 (xor_8_out, pozisyon_7_out_7, pozisyon_7_out_9);
  xor xor_9 (xor_9_out, pozisyon_8_out_7, pozisyon_8_out_9);
  and and_1 (and_1_out, xor_2_out, xor_9_out, xor_8_out);
  and and_2 (and_2_out, xor_7_out, xor_6_out, xor_5_out);
  and and_3 (and_3_out, xor_4_out, xor_3_out, xor_1_out);
  xor xor_10 (xor_10_out, xor_1_out, xor_3_out);
  xor xor_11 (xor_11_out, xor_4_out, xor_5_out);
  xor xor_12 (xor_12_out, xor_6_out, xor_7_out);
  xor xor_13 (xor_13_out, xor_8_out, xor_9_out);
  and and_4 (and_4_out, ganador_1_out_10, ganador_2_out_10);
  and and_5 (and_5_out, and_1_out, and_2_out, and_3_out);
  xor xor_14 (xor_14_out, xor_10_out, xor_11_out);
  xor xor_15 (xor_15_out, xor_12_out, xor_13_out);
  and and_6 (out_12, and_4_out, and_5_out);
  xor xor_16 (xor_16_out, xor_14_out, xor_15_out);
  xor xor_17 (xor_17_out, xor_16_out, xor_2_out);
  not not_3 (not_3_out, xor_17_out);
endmodule

module ganador (
  input  _3,
  input  _2,
  input  _1,
  input  _6,
  input  _5,
  input  _4,
  input  _9,
  input  _8,
  input  _7,
  output out_10
);

  wire and_1_out, and_2_out, and_3_out, and_4_out, and_5_out, and_6_out, and_7_out, and_8_out, or_1_out,
       or_2_out, or_3_out;

  and and_1 (and_1_out, _3, _2, _1);
  and and_2 (and_2_out, _6, _5, _4);
  and and_3 (and_3_out, _9, _8, _7);
  and and_4 (and_4_out, _1, _4, _7);
  and and_5 (and_5_out, _2, _5, _8);
  and and_6 (and_6_out, _3, _6, _9);
  and and_7 (and_7_out, _1, _5, _9);
  and and_8 (and_8_out, _3, _5, _7);
  or or_1 (or_1_out, and_1_out, and_2_out, and_3_out, and_4_out);
  or or_2 (or_2_out, and_5_out, and_6_out, and_7_out, and_8_out);
  or or_3 (or_3_out, or_1_out, or_2_out);
  not not_1 (out_10, or_3_out);

  // Notes on the sheet:
  //   321
  //   654
  //   987
  //   147
  //   258
  //   349
  //   159
  //   357
endmodule
